# Fritzing sketch programator_at89c2051 (saved by Fritzing 0.9.3b)
breadboards: 1

parts:
  IC1 = IC, DIP package, 20 pins [chip_label=IC]
  Часть1 = Arduino Uno (Rev3)
  KY-1 = Keyes Relay [package=THT]
  Power_plug1 = Power plug

nets:
  N1: IC1.pin1, KY-1.C
  N2: IC1.pin5, Часть1.D4
  N3: IC1.pin6, Часть1.D2
  N4: IC1.pin7, Часть1.A0
  N5: IC1.pin8, Часть1.A1
  N6: IC1.pin9, Часть1.A2
  GND: IC1.pin10, Часть1.GND, KY-1.ground, Power_plug1.GND
  N7: IC1.pin11, Часть1.A3
  N8: IC1.pin12, Часть1.D5_PWM
  N9: IC1.pin13, Часть1.D6_PWM
  N10: IC1.pin14, Часть1.D7
  N11: IC1.pin15, Часть1.D8
  N12: IC1.pin16, Часть1.D9_PWM
  N13: IC1.pin17, Часть1.D10_PWM/SS
  N14: IC1.pin18, Часть1.D11_PWM/MOSI
  N15: IC1.pin19, Часть1.D12/MISO
  N16: IC1.pin20, Часть1.5V, KY-1.power
  N17: Часть1.A4/SDA, KY-1.signal
  N18: Часть1.D3_PWM, KY-1.NC
  N19: KY-1.NO, Power_plug1.VCC

notes:
  12v
  at89c2051

custom parts:
  Keyes Relay: The Keyes 5V relay module is suitable for SCM development, home appliance control. It uses a 5V~12V TIL control signal which can control DC / AC signal.
